# Fritzing sketch NerfDoor (saved by Fritzing 0.9.2b)
circuit board: 27.3093cm x 8.18928cm
stripboards: 3
breadboards: 1

parts:
  J4 = female pin header, 2 pins [form="♀ (female)"]
  USB_cable_(power_and_signal_line) = USB Connectors [package=usb-a-h]
  U1 = atmega328 [package=dip]
  R1 = Resistor [tolerance=±5% resistance=10k package=THT]
  R2 = Resistor [tolerance=±5% resistance=560 package=THT]
  User = Pushbutton [package=THT]
  LED7 = LED - 5mm [color="Green (555nm)" package="5 mm [THT]"]
  J5 = female pin header, 2 pins [form="♀ (female)"]
  R3 = Resistor [tolerance=±5% resistance=560 package=THT]
  LED1 = LED - 3mm [color="White (6500K)" package="3 mm [THT]"]
  USB_Hub_(modified_D+_used_as_signal_line) = USB Connectors [package=usb-a-s]
  LED3 = LED - 3mm [color="White (6500K)" package="3 mm [THT]"]
  J3 = female pin header, 3 pins [form="♀ (female)"]
  JP2 = Header 12 [package=1x12_machine-pin-header_lock.004]
  LED2 = LED - 3mm [color="White (6500K)" package="3 mm [THT]"]
  Door = Pushbutton [package=THT]
  J1 = Basic Servo
  LED4 = LED - 3mm [color="White (6500K)" package="3 mm [THT]"]
  Override_(Leave_room_safely) = Pushbutton [package=THT]
  LED6 = LED - 5mm [color="Red (633nm)" package="5 mm [THT]"]
  LED5 = LED - 3mm [color="White (6500K)" package="3 mm [THT]"]
  JP1 = Header 12 [package=1x12_machine-pin-header_lock.004]
  Raspberry_Pi1 = Raspberry Pi B rev2

nets:
  VCC: J4.pin1, J4.pin2, USB_cable_(power_and_signal_line).VBUS, U1.VCC, USB_Hub_(modified_D+_used_as_signal_line).VBUS, J3.pin2, J1.vcc
  N1: USB_cable_(power_and_signal_line).D+, U1.D2, R1.Pin_0, J5.pin1, USB_Hub_(modified_D+_used_as_signal_line).D+, JP1.7, Raspberry_Pi1.GPIO_10
  GND: USB_cable_(power_and_signal_line).GND, U1.GND, R1.Pin_1, J5.pin2, USB_Hub_(modified_D+_used_as_signal_line).GND, J3.pin1, JP2.2, JP2.4, JP2.6, JP2.8, JP2.10, JP2.12, J1.gnd, Override_(Leave_room_safely).leg1, JP1.2, JP1.4, JP1.6, JP1.8, JP1.10, JP1.12
  N2: U1.D3_(PWM), Override_(Leave_room_safely).leg0, JP1.9
  N3: U1.D13, J3.pin3, J1.pulse, JP1.1
  N4: R2.Pin_0, LED7.anode
  N5: R2.Pin_1, Raspberry_Pi1.GPIO_25
  N6: User.leg0, LED7.cathode, LED1.cathode, LED3.cathode, LED2.cathode, Door.leg1, LED4.cathode, LED6.cathode, LED5.cathode, Raspberry_Pi1.GND, Raspberry_Pi1.GPIO_18
  N7: User.leg1, Raspberry_Pi1.GPIO_2
  N8: R3.Pin_0, LED6.anode
  N9: R3.Pin_1, Raspberry_Pi1.GPIO_24
  N10: LED1.anode, Raspberry_Pi1.GPIO_22
  N11: LED3.anode, Raspberry_Pi1.GPIO_4
  N12: LED2.anode, Raspberry_Pi1.GPIO_17, Raspberry_Pi1.3V3
  N13: Door.leg0, Raspberry_Pi1.GPIO_3
  N14: LED4.anode, Raspberry_Pi1.GPIO_23
  N15: LED5.anode, Raspberry_Pi1.GPIO_27

custom parts:
  atmega328: Atmel ATmega328 microcontroller.
